# Fritzing sketch pill reminder FInal Schematic (saved by Fritzing 0.9.2b)
breadboards: 1

parts:
  U1 = atmega328 [package=dip]
  R1 = Resistor [tolerance=±5% resistance=10k package=THT]
  VCC1 = Battery
  XTAL1 = Crystal [frequency="16 Mhz" package=SMD]
  22_pF = Capacitor [package=cap-pth-small2]
  VCC2 = Battery
  22_pF_2 = Capacitor [package=cap-pth-small2]
  ZS-042_RTC1 = ZS-042 RTC Module
  Diode = Rectifier Diode [package="Melf DO-213 AA [SMD]"]
  Main_On/Off_Switch = Toggle Switch [package=THT]
  Diode_2 = Rectifier Diode [package="Melf DO-213 AA [SMD]"]
  DIP_Switch_(12_Pins) = DIP Switch 8 Position [package=dipswitch-08]
  SW1 = DIP SWITCH [package=dipswitch-02]
  SW2 = DIP SWITCH [package=dipswitch-02]
  R2 = Resistor [tolerance=±5% resistance=150k package=THT]
  R3 = Resistor [tolerance=±5% resistance=150k package=THT]
  R4 = Resistor [tolerance=±5% resistance=150k package=THT]
  R5 = Resistor [tolerance=±5% resistance=150k package=THT]
  R6 = Resistor [tolerance=±5% resistance=150k package=THT]
  R7 = Resistor [tolerance=±5% resistance=150k package=THT]
  R8 = Resistor [tolerance=±5% resistance=150k package=THT]
  R9 = Resistor [tolerance=±5% resistance=150k package=THT]
  R10 = Resistor [tolerance=±5% resistance=150k package=THT]
  R11 = Resistor [tolerance=±5% resistance=150k package=THT]
  R12 = Resistor [tolerance=±5% resistance=150k package=THT]
  R13 = Resistor [tolerance=±5% resistance=150k package=THT]
  R14 = Resistor [tolerance=±5% resistance=10k package=THT]
  R15 = Resistor [tolerance=±5% resistance=220 package=THT]
  R16 = Resistor [tolerance=±5% resistance=150k package=THT]
  0_1_uF = Capacitor [package=cap-pth-small2]
  Device_lid_open/close_detection_system = Toggle Switch [package=THT]
  R17 = Resistor [tolerance=±5% resistance=150k package=THT]
  Piezo_Buzzer = Piezo Speaker
  R18 = Resistor [tolerance=±5% resistance=150k package=THT]
  Missed_Pill_Indicator_LED = LED - 3mm [color="Red (633nm)" package="3 mm [THT]"]
  R19 = Resistor [tolerance=±5% resistance=220 package=THT]
  R20 = Resistor [tolerance=±5% resistance=150k package=THT]

nets:
  N1: U1.RESET, R1.Pin_1
  N2: U1.D2, SW1.4, R8.Pin_1
  N3: U1.D3_(PWM), SW1.3, R5.Pin_1
  N4: U1.D4, DIP_Switch_(12_Pins).16, R4.Pin_1
  N5: U1.VCC, U1.AVCC, R1.Pin_0, Diode.cathode, R14.Pin_0
  GND: U1.GND, VCC1.-, 22_pF.1, 22_pF_2.1, ZS-042_RTC1.GND, R2.Pin_0, R3.Pin_0, R4.Pin_0, R5.Pin_0, R6.Pin_0, R7.Pin_0, R8.Pin_0, R9.Pin_1, R10.Pin_1, R11.Pin_1, R12.Pin_1, R13.Pin_1, R16.Pin_1, 0_1_uF.1, R17.Pin_1, Piezo_Buzzer.pin2, R18.Pin_1, Missed_Pill_Indicator_LED.cathode, R20.Pin_1
  N6: U1.XLAT1, XTAL1.pin_0, 22_pF_2.2
  N7: U1.XLAT2, XTAL1.pin_1, 22_pF.2
  N8: U1.D5_(PWM), DIP_Switch_(12_Pins).15, R3.Pin_1
  N9: U1.D6_(PWM), DIP_Switch_(12_Pins).14, R2.Pin_1
  N10: U1.D7, DIP_Switch_(12_Pins).13, R6.Pin_1
  N11: U1.D8, DIP_Switch_(12_Pins).12, R7.Pin_1
  N12: U1.D9_(PWM), DIP_Switch_(12_Pins).11, R10.Pin_0
  N13: U1.D10_(PWM), DIP_Switch_(12_Pins).10, R13.Pin_0
  N14: U1.D11_(PWM), DIP_Switch_(12_Pins).9, R9.Pin_0
  N15: U1.D12, SW2.4, R11.Pin_0
  N16: U1.D13, SW2.3, R12.Pin_0
  N17: U1.A0, R15.Pin_0, R16.Pin_0
  N18: U1.A1, Device_lid_open/close_detection_system.COM, R17.Pin_0
  N19: U1.A2, Piezo_Buzzer.pin1, R18.Pin_0
  N20: U1.A3, R19.Pin_0, R20.Pin_0
  N21: U1.A4, ZS-042_RTC1.SDA
  N22: U1.A5, ZS-042_RTC1.SCL
  N23: VCC1.+, VCC2.-
  N24: VCC2.+, Main_On/Off_Switch.COM
  N25: ZS-042_RTC1.VCC, R15.Pin_1, 0_1_uF.2
  N26: Diode.anode, Diode_2.cathode
  N27: Main_On/Off_Switch.L2, Diode_2.anode
  N28: DIP_Switch_(12_Pins).1, DIP_Switch_(12_Pins).2, DIP_Switch_(12_Pins).3, DIP_Switch_(12_Pins).4, DIP_Switch_(12_Pins).5, DIP_Switch_(12_Pins).6, DIP_Switch_(12_Pins).7, DIP_Switch_(12_Pins).8, SW1.1, SW1.2, SW2.1, SW2.2, R14.Pin_1

notes:
  FINAL SCHEMATIC
  (Developed by Sourav Paul)

// code stored in the sketch: Untitled2.ino
 //ARDUINO CODE FOR PILL REMINDER DEVICE
 //Developed by Sourav Paul

#include <Wire.h>
#include "RTClib.h"
#include <avr/sleep.h>
#include <avr/wdt.h>
#include <avr/power.h>


const int clockPower = 14; //RTC module VCC power fed from Atmega328P IC Pin
const int boxOpenPin = 15; //device top lid open / close detection pin
const int buzzerPin = 16; // buzzer for Alarm
const int ledPin = 17; // led for missed pill indicator


RTC_DS1307 rtc;  //Real-Time Clock module declaration
DateTime now;
boolean boxOpened = false;
boolean ledOn = false;
// watchdog interrupt
ISR (WDT_vect)
{
  wdt_disable();  // disable watchdog
}  // end of WDT_vect

void setup() {
 //Begin RTC and adjust initial time
  toggleRTCPower(true);
  //Set pins as user input
  for (int digitalPin=2; digitalPin<=17; digitalPin++)
  {
    pinMode(digitalPin, INPUT);
  }

}

void loop() {
  sleep(); // 2 secs sleep to save power thus increasing battery life
 
  ledAlertOff(); // turn off led missed pill indicator alert if it is already on
 
  toggleRTCPower(false);
 
  //check for user scheduled alarm time through 12 pins DIP switch
  checkTime(2,23,30,0,30);    //12 AM

  //loop for check time from @2 AM to @10 PM at 2 hours interval
  for(int pinCounter=3, timeCounter=0; pinCounter<=13; pinCounter++)   
     {
       checkTime(pinCounter,++timeCounter, 30,++timeCounter,30 ); 
     }
}

//function to turn LED missed pill indiactor alarm off
void ledAlertOff()
{
   if(ledOn == true && digitalRead(boxOpenPin) == HIGH)
  {
      digitalWrite(ledPin, LOW);
      pinMode(ledPin, INPUT);
      ledOn = false;
  }
}

//method to check for current time through RTC and turn on buzzer alert if device top lid is not opened
void checkTime(int pin, int minHr, int minMin, int maxHr, int maxMin)
{
  if (digitalRead(pin) == HIGH)
  {
    if ((now.hour() == minHr && now.minute() > minMin) || (now.hour() == maxHr && now.minute() < maxMin)) //check the boxOpenPin status within the 30 mins interval of user scheduled time
    {
      if (digitalRead(boxOpenPin) == HIGH) // check whether boxOpenPin is HIGH through device top lid open/close system 
      {
        boxOpened = true;
      }
    }
    if (now.hour() == maxHr && now.minute() >= maxMin && now.minute() < (maxMin + 5) &&  boxOpened == false )
    {
      alarm();
    }
  }
  if (now.hour() == maxHr && now.minute() >= (maxMin + 5))
  {
    boxOpened = false;
  }
}

//function to give alarm sound through the buzzer
void alarm() // currently duration set for 5 mins or 300 secs
{
  for (int timeLoop=1; timeLoop<=150; timeLoop++)
  {
    pinMode(buzzerPin, OUTPUT);
    digitalWrite(buzzerPin, HIGH);
    delay(2000);
    //stop alarm
    if (digitalRead(boxOpenPin) == HIGH)
    {
      digitalWrite(buzzerPin, LOW);
      for (int remainingLoop=1; remainingLoop<=(150-timeLoop); remainingLoop++)
      {
       ledAlertOff();
       sleep(); // sleeps for 2 secs interval
      }
      break;
    }
 // Turn on LED missed pill indicator
    if(timeLoop == 150)
    {
      pinMode(ledPin, OUTPUT);
      digitalWrite(ledPin, HIGH);
      ledOn = true;
    }
  }
  pinMode(buzzerPin, INPUT);
}

//sleep code
void sleep()
{
  // disable ADC
  ADCSRA = 0;
  // clear various "reset" flags
  MCUSR = 0;
  // allow changes, disable reset
  WDTCSR = bit (WDCE) | bit (WDE);
  // set interrupt mode and an interval 
  WDTCSR = bit (WDIE) | bit (WDP2) | bit (WDP1) | bit (WDP0);    // set WDIE, and 2 seconds delay
  wdt_reset();  // pat the dog
  set_sleep_mode (SLEEP_MODE_PWR_DOWN);
  noInterrupts ();           // timed sequence follows
  sleep_enable();
  // turn off brown-out enable in software
  MCUCR = bit (BODS) | bit (BODSE);
  MCUCR = bit (BODS);
  interrupts ();             // guarantees next instruction executed
  sleep_cpu ();
  // cancel sleep as a precaution
  sleep_disable();
}

//Toggle power to the RTC VCC pin through Atmega328P IC pin
void toggleRTCPower(boolean resetRTC)
{
// power up RTC clock chip
 pinMode (clockPower, OUTPUT);
 digitalWrite (clockPower, HIGH);

 // activate I2C
  Wire.begin();

  if(resetRTC == true)
  {
  rtc.begin(); // Start the RTC library code
  // June 20, 2016, 10PM is set as initial date and time (24 hours format used)
  rtc.adjust(DateTime(2016, 6, 20, 22, 0, 0));
  }
 // find the time  
 now = rtc.now();

 // finished with clock
 digitalWrite (clockPower, LOW);
 pinMode (clockPower, INPUT);

 // turn off I2C
  TWCR &= ~(bit(TWEN) | bit(TWIE) | bit(TWEA));

  // turn off I2C pull-ups
  digitalWrite (A4, LOW);
  digitalWrite (A5, LOW);


}
